// Digital circuit design.dig as structural Verilog
module \design  (
  input  clk
);

  wire R_W;
  wire [7:0] D_i, D_o;
  wire [15:0] A;

  EEPROMDualPort #(.AddrBits(16), .Bits(8)) eepromdualport_1 (.A(A), .Din(D_o), .str(R_W), .C(clk), .ld(1'b1), .D(D_i));
  a_risc a_risc_1 (.c(clk), .D_i(D_i), .R_W(R_W), .D_o(D_o), .A(A));

  // Other names for the same wires on the sheet: C = clk

  // Notes on the sheet:
  //   clk: Hz: 16
  //   contents of eepromdualport_1 (hex, n*v repeats v):
  //   15,6,25,9,30,12,58,1e,e9,15,57,fffffffffffffff6
endmodule
